# Fritzing sketch light_dependend_resistor (saved by Fritzing 0.9.0b)
breadboards: 1

parts:
  R1 = Photocell (LDR) [package=THT]
  R2 = Resistor [tolerance=±5% resistance=10k package=THT]
  Bauteil1 = Arduino Uno (Rev3)

nets:
  N1: R1.pin_0, Bauteil1.5V
  N2: R1.pin_1, R2.Pin_0, Bauteil1.A0
  N3: R2.Pin_1, Bauteil1.GND
